# Fritzing sketch FSR (saved by Fritzing 0.8.3b)
breadboards: 2

parts:
  J1 = Basic Force Sensing Resistor (FSR) [package=THT]
  パーツ1 = Arduino Uno (Rev3)
  R1 = Resistor [tolerance=±5% resistance=220 package=THT]
  LCD1 = LCD screen
  R2 = Resistor [tolerance=±5% resistance=220 package=THT]
  R3 = Trimmer Potentiometer [maximum_resistance=10kΩ package=THT]

nets:
  N1: J1.pin_0, パーツ1.GND
  N2: J1.pin_1, パーツ1.A0, R1.Pin_0
  N3: パーツ1.ICSP_MISO, パーツ1.D12/MISO, LCD1.E
  N4: パーツ1.ICSP_MOSI, パーツ1.D11_PWM/MOSI, LCD1.DB1
  N5: パーツ1.D2, LCD1.LED-
  N6: パーツ1.D3_PWM, LCD1.LED+
  N7: パーツ1.D4, LCD1.DB7
  N8: パーツ1.D5_PWM, LCD1.DB6
  N9: パーツ1.5V, R1.Pin_1
  N10: LCD1.VSS, R2.Pin_0
  N11: LCD1.VDD, LCD1.V0, LCD1.DB0, R3.leg1
  N12: LCD1.RS, R2.Pin_1, R3.leg2
  N13: LCD1.R/W, R3.wiper
