# Fritzing sketch FSR_BEEP_AND_LCD (saved by Fritzing 0.8.5b)
breadboards: 2

parts:
  LCD1 = LCD screen
  R2 = Resistor [tolerance=±5% resistance=220 package=THT]
  R3 = Trimmer Potentiometer [maximum_resistance=10kΩ package=THT]
  パーツ1 = Arduino Uno (Rev3)
  LED1 = LED - 5mm [color="Red (633nm)" package="5 mm [THT]"]
  LED2 = LED - 5mm [color="Blue (470nm)" package="5 mm [THT]"]
  LED3 = LED - 5mm [color="Yellow (592nm)" package="5 mm [THT]"]
  J1 = Piezo Speaker
  J2 = Basic Force Sensing Resistor (FSR) [package=THT]
  R4 = Resistor [tolerance=±5% resistance=220 package=THT]

nets:
  N1: LCD1.VSS, R2.Pin_0
  VDD: LCD1.VDD, LCD1.V0, LCD1.DB0, R3.leg1, パーツ1.3V3, LED1.cathode, LED2.cathode, LED3.cathode, J1.pin1, J2.pin_0, J2.pin_1, R4.Pin_0
  N2: LCD1.RS, R2.Pin_1, R3.leg2, パーツ1.5V
  N3: LCD1.R/W, R3.wiper
  N4: LCD1.E, パーツ1.D12/MISO
  N5: LCD1.DB1, パーツ1.D11_PWM/MOSI
  N6: LCD1.DB6, パーツ1.D5_PWM
  N7: LCD1.DB7, パーツ1.D4
  N8: LCD1.LED+, パーツ1.D3_PWM
  N9: LCD1.LED-, パーツ1.D2
  N10: パーツ1.A0, R4.Pin_1
  N11: パーツ1.D8, J1.pin2
  N12: パーツ1.D9_PWM, LED2.anode
  N13: パーツ1.D10_PWM/SS, LED3.anode
  N14: パーツ1.D13/SCK, LED1.anode
